// Logisim project ALU.circ as structural Verilog: 17 circuits, main circuit ALU32
module LeftShift32 (
  input  [31:0] B,
  input  [4:0] Sa,
  input  Cin,
  output [31:0] C
);

  wire [31:0] multiplexer_1_out, multiplexer_2_out, multiplexer_3_out, multiplexer_4_out, shift_1_bit_1_c,
       shift_2_bit_1_c, shift_4_bit_1_c, shift_8_bit_1_c, shift_16_bit_1_c;

  shift_1_bit shift_1_bit_1 (.Cin(Cin), .B(B), .C(shift_1_bit_1_c));
  Multiplexer #(.width(32), .enable("false")) multiplexer_1 (
    .in0(B), .in1(shift_1_bit_1_c), .out(multiplexer_1_out), .sel(Sa[0]));
  shift_2_bit shift_2_bit_1 (.Cin(Cin), .B(multiplexer_1_out), .C(shift_2_bit_1_c));
  Multiplexer #(.width(32), .enable("false")) multiplexer_2 (
    .in0(multiplexer_1_out), .in1(shift_2_bit_1_c), .out(multiplexer_2_out), .sel(Sa[1]));
  shift_4_bit shift_4_bit_1 (.Cin(Cin), .B(multiplexer_2_out), .C(shift_4_bit_1_c));
  Multiplexer #(.width(32), .enable("false")) multiplexer_3 (
    .in0(multiplexer_2_out), .in1(shift_4_bit_1_c), .out(multiplexer_3_out), .sel(Sa[2]));
  shift_8_bit shift_8_bit_1 (.Cin(Cin), .B(multiplexer_3_out), .C(shift_8_bit_1_c));
  Multiplexer #(.width(32), .enable("false")) multiplexer_4 (
    .in0(multiplexer_3_out), .in1(shift_8_bit_1_c), .out(multiplexer_4_out), .sel(Sa[3]));
  shift_16_bit shift_16_bit_1 (.Cin(Cin), .B(multiplexer_4_out), .C(shift_16_bit_1_c));
  Multiplexer #(.width(32), .enable("false")) multiplexer_5 (
    .in0(multiplexer_4_out), .in1(shift_16_bit_1_c), .out(C), .sel(Sa[4]));
endmodule

module Add32 (
  input  [31:0] A,
  input  [31:0] B,
  input  Cin,
  output [31:0] C,
  output V
);

  wire add16_1_cout, add16_2_cout, add16_2_v;

  add16 add16_1 (.A(A[15:0]), .B(B[15:0]), .Cin(Cin), .C(C[15:0]), .Cout(add16_1_cout));  // open: V
  add16 add16_2 (.A(A[31:16]), .B(B[31:16]), .Cin(add16_1_cout), .C(C[31:16]), .Cout(add16_2_cout), .V(add16_2_v));
  xor xor_1 (V, add16_2_cout, add16_2_v);
endmodule

module ALU32 (
  input  [31:0] A,
  input  [31:0] B,
  input  [3:0] Op,
  input  [4:0] Sa,
  output [31:0] C,
  output V
);

  wire [31:0] arithmetic_ops_1_c, comparison_1_c, logical_ops_1_c, shift_ops_1_c;

  Logical_Ops logical_ops_1 (.A(A), .B(B), .Op(Op), .C(logical_ops_1_c));
  Comparison comparison_1 (.B(B), .A(A), .Op(Op), .C(comparison_1_c));
  Shift_Ops shift_ops_1 (.B(B), .Op(Op), .Sa(Sa), .C(shift_ops_1_c));
  Arithmetic_Ops arithmetic_ops_1 (.A(A), .B(B), .Op(Op), .C(arithmetic_ops_1_c), .V(V));
  assign C = logical_ops_1_c | comparison_1_c | arithmetic_ops_1_c | shift_ops_1_c;  // OR_Gate or_1, 32 bits wide
endmodule

module shift_1_bit (
  input  Cin,
  input  [31:0] B,
  output [31:0] C
);


  assign C = {B[30:0], Cin};
endmodule

module shift_2_bit (
  input  Cin,
  input  [31:0] B,
  output [31:0] C
);

  wire [31:0] shift_1_bit_1_c;

  shift_1_bit shift_1_bit_1 (.Cin(Cin), .B(B), .C(shift_1_bit_1_c));
  shift_1_bit shift_1_bit_2 (.Cin(Cin), .B(shift_1_bit_1_c), .C(C));
endmodule

module shift_4_bit (
  input  Cin,
  input  [31:0] B,
  output [31:0] C
);

  wire [31:0] shift_2_bit_1_c;

  shift_2_bit shift_2_bit_1 (.Cin(Cin), .B(B), .C(shift_2_bit_1_c));
  shift_2_bit shift_2_bit_2 (.Cin(Cin), .B(shift_2_bit_1_c), .C(C));
endmodule

module shift_8_bit (
  input  Cin,
  input  [31:0] B,
  output [31:0] C
);

  wire [31:0] shift_4_bit_1_c;

  shift_4_bit shift_4_bit_1 (.Cin(Cin), .B(B), .C(shift_4_bit_1_c));
  shift_4_bit shift_4_bit_2 (.Cin(Cin), .B(shift_4_bit_1_c), .C(C));
endmodule

module shift_16_bit (
  input  Cin,
  input  [31:0] B,
  output [31:0] C
);

  wire [31:0] shift_8_bit_1_c;

  shift_8_bit shift_8_bit_1 (.Cin(Cin), .B(B), .C(shift_8_bit_1_c));
  shift_8_bit shift_8_bit_2 (.Cin(Cin), .B(shift_8_bit_1_c), .C(C));
endmodule

module shift_32_bit (
  input  Cin,
  input  [31:0] B,
  input  [4:0] Sa,
  output [31:0] C
);

  wire [31:0] multiplexer_1_out, multiplexer_2_out, multiplexer_3_out, multiplexer_4_out, shift_1_bit_1_c,
       shift_2_bit_1_c, shift_4_bit_1_c, shift_8_bit_1_c, shift_16_bit_1_c;

  shift_1_bit shift_1_bit_1 (.Cin(Cin), .B(B), .C(shift_1_bit_1_c));
  Multiplexer #(.width(32), .enable("false")) multiplexer_1 (
    .in0(B), .in1(shift_1_bit_1_c), .out(multiplexer_1_out), .sel(Sa[0]));
  shift_2_bit shift_2_bit_1 (.Cin(Cin), .B(multiplexer_1_out), .C(shift_2_bit_1_c));
  Multiplexer #(.width(32), .enable("false")) multiplexer_2 (
    .in0(multiplexer_1_out), .in1(shift_2_bit_1_c), .out(multiplexer_2_out), .sel(Sa[1]));
  shift_4_bit shift_4_bit_1 (.Cin(Cin), .B(multiplexer_2_out), .C(shift_4_bit_1_c));
  Multiplexer #(.width(32), .enable("false")) multiplexer_3 (
    .in0(multiplexer_2_out), .in1(shift_4_bit_1_c), .out(multiplexer_3_out), .sel(Sa[2]));
  shift_8_bit shift_8_bit_1 (.Cin(Cin), .B(multiplexer_3_out), .C(shift_8_bit_1_c));
  Multiplexer #(.width(32), .enable("false")) multiplexer_4 (
    .in0(multiplexer_3_out), .in1(shift_8_bit_1_c), .out(multiplexer_4_out), .sel(Sa[3]));
  shift_16_bit shift_16_bit_1 (.Cin(Cin), .B(multiplexer_4_out), .C(shift_16_bit_1_c));
  Multiplexer #(.width(32), .enable("false")) multiplexer_5 (
    .in0(multiplexer_4_out), .in1(shift_16_bit_1_c), .out(C), .sel(Sa[4]));
endmodule

// 1 bit FA
module add1 (
  input  B,
  input  A,
  input  Cin,
  output C,
  output Cout
);

  wire and_1_out, and_2_out, xor_1_out;

  xor xor_1 (xor_1_out, B, A);
  xor xor_2 (C, xor_1_out, Cin);
  and and_1 (and_1_out, Cin, xor_1_out);
  and and_2 (and_2_out, B, A);
  or or_1 (Cout, and_1_out, and_2_out);
endmodule

module add4 (
  input  [3:0] A,
  input  [3:0] B,
  input  Cin,
  output [3:0] C,
  output Cout,
  output V
);

  wire add1_1_cout, add1_2_cout;

  add1 add1_1 (.B(B[0]), .A(A[0]), .Cin(Cin), .C(C[0]), .Cout(add1_1_cout));
  add1 add1_2 (.B(B[1]), .A(A[1]), .Cin(add1_1_cout), .C(C[1]), .Cout(add1_2_cout));
  add1 add1_3 (.B(B[2]), .A(A[2]), .Cin(add1_2_cout), .C(C[2]), .Cout(V));
  add1 add1_4 (.B(B[3]), .A(A[3]), .Cin(V), .C(C[3]), .Cout(Cout));

  // Notes on the sheet:
  //   4 bits adder
endmodule

module add16 (
  input  [15:0] A,
  input  [15:0] B,
  input  Cin,
  output [15:0] C,
  output Cout,
  output V
);

  wire add4_1_cout, add4_2_cout, add4_3_cout;

  add4 add4_1 (.A(A[3:0]), .B(B[3:0]), .Cin(Cin), .C(C[3:0]), .Cout(add4_1_cout));  // open: V
  add4 add4_2 (.A(A[7:4]), .B(B[7:4]), .Cin(add4_1_cout), .C(C[7:4]), .Cout(add4_2_cout));  // open: V
  add4 add4_3 (.A(A[11:8]), .B(B[11:8]), .Cin(add4_2_cout), .C(C[11:8]), .Cout(add4_3_cout));  // open: V
  add4 add4_4 (.A(A[15:12]), .B(B[15:12]), .Cin(add4_3_cout), .C(C[15:12]), .Cout(Cout), .V(V));
endmodule

module Logical_Ops (
  input  [31:0] A,
  input  [31:0] B,
  input  [3:0] Op,
  output [31:0] C
);

  wire and_1_out, or_2_out;
  wire [1:1] and_2_out;
  wire [31:0] and_3_out, nor_1_out, or_1_out, xor_1_out;

  and and_1 (and_1_out, ~Op[3], Op[2], ~Op[1]);  // AND_Gate
  and and_2 (and_2_out[1], Op[3], ~Op[2], Op[1]);  // AND_Gate
  assign and_3_out = A & B;  // AND_Gate and_3, 32 bits wide
  assign or_1_out = A | B;  // OR_Gate or_1, 32 bits wide
  assign xor_1_out = A ^ B;  // XOR_Gate xor_1, 32 bits wide
  assign nor_1_out = ~(A | B);  // NOR_Gate nor_1, 32 bits wide
  or or_2 (or_2_out, and_1_out, and_2_out[1]);
  Multiplexer #(.select(2), .width(32)) multiplexer_1 (
    .in0(and_3_out), .in1(or_1_out), .in2(xor_1_out), .in3(nor_1_out), .out(C), .sel({and_2_out[1], Op[0]}),
    .en(or_2_out));
endmodule

module Comparison (
  input  [31:0] B,
  input  [31:0] A,
  input  [3:0] Op,
  output [31:0] C
);

  wire and_3_out, and_7_out, and_8_out, and_9_out, not_2_out, not_3_out, or_1_out;
  wire [1:0] and_5_out, and_6_out;
  wire [1:1] and_4_out;
  wire [7:0] and_1_out, and_2_out;
  wire [31:0] bit_extender_1_out, bit_extender_2_out, bit_extender_3_out, bit_extender_4_out, not_1_out,
       xnor_1_out;

  assign xnor_1_out = ~(B ^ A);  // XNOR_Gate xnor_1, 32 bits wide
  assign not_1_out = ~A;  // NOT_Gate not_1, 32 bits wide
  assign and_1_out = xnor_1_out[7:0] & xnor_1_out[15:8] & xnor_1_out[23:16] & xnor_1_out[31:24];  // AND_Gate and_1, 8 bits wide
  assign and_2_out = not_1_out[7:0] & not_1_out[15:8] & not_1_out[23:16] & not_1_out[31:24];  // AND_Gate and_2, 8 bits wide
  and and_3 (and_3_out, Op[3], ~Op[2], ~Op[1]);  // AND_Gate
  and and_4 (and_4_out[1], Op[3], Op[2], Op[1]);
  assign and_5_out = and_1_out[1:0] & and_1_out[3:2] & and_1_out[5:4] & and_1_out[7:6];  // AND_Gate and_5, 2 bits wide
  assign and_6_out = and_2_out[1:0] & and_2_out[3:2] & and_2_out[5:4] & and_2_out[7:6];  // AND_Gate and_6, 2 bits wide
  or or_1 (or_1_out, and_3_out, and_4_out[1]);
  and and_7 (and_7_out, and_6_out[0], and_6_out[1]);
  and and_8 (and_8_out, and_5_out[0], and_5_out[1]);
  and and_9 (and_9_out, ~A[31], ~and_7_out);  // AND_Gate
  not not_2 (not_2_out, and_8_out);
  not not_3 (not_3_out, and_9_out);
  assign bit_extender_1_out = {{31{1'b0}}, not_2_out};  // Bit_Extender bit_extender_1
  assign bit_extender_2_out = {{31{1'b0}}, and_8_out};  // Bit_Extender bit_extender_2
  assign bit_extender_3_out = {{31{1'b0}}, not_3_out};  // Bit_Extender bit_extender_3
  assign bit_extender_4_out = {{31{1'b0}}, and_9_out};  // Bit_Extender bit_extender_4
  Multiplexer #(.select(2), .width(32)) multiplexer_1 (
    .in0(bit_extender_1_out), .in1(bit_extender_2_out), .in2(bit_extender_3_out), .in3(bit_extender_4_out),
    .out(C), .sel({and_4_out[1], Op[0]}), .en(or_1_out));
endmodule

module Arithmetic_Ops (
  input  [31:0] A,
  input  [31:0] B,
  input  [3:0] Op,
  output [31:0] C,
  output V
);

  wire and_1_out, and_4_out;
  wire [31:0] and_2_out, and_3_out, bit_extender_1_out, multiplexer_1_out, not_1_out;

  Multiplexer #(.width(32), .enable("false")) multiplexer_1 (
    .in0(B), .in1(not_1_out), .out(multiplexer_1_out), .sel(Op[2]));
  assign not_1_out = ~B;  // NOT_Gate not_1, 32 bits wide
  and and_1 (and_1_out, Op[1], ~Op[3]);  // AND_Gate
  assign bit_extender_1_out = {{31{and_1_out}}, and_1_out};  // Bit_Extender bit_extender_1
  assign and_2_out = A & bit_extender_1_out;  // AND_Gate and_2, 32 bits wide
  assign and_3_out = bit_extender_1_out & multiplexer_1_out;  // AND_Gate and_3, 32 bits wide
  and and_4 (and_4_out, and_1_out, Op[2]);
  Add32 add32_1 (.A(and_2_out), .B(and_3_out), .Cin(and_4_out), .C(C), .V(V));

  // Notes on the sheet:
  //   B
endmodule

module Shift_Ops (
  input  [31:0] B,
  input  [3:0] Op,
  input  [4:0] Sa,
  output [31:0] C
);

  wire and_1_out, and_2_out, and_3_out, and_4_out, or_1_out, reversed_1_sign_bit;
  wire [4:0] and_5_out, bit_extender_1_out;
  wire [31:0] leftshift32_1_c, multiplexer_1_out, reversed_1_b_reversed, reversed_2_b_reversed;

  Reversed reversed_1 (.B(B), .B_reversed(reversed_1_b_reversed), .Sign_bit(reversed_1_sign_bit));
  and and_1 (and_1_out, ~Op[1], ~Op[2], ~Op[3]);  // AND_Gate
  and and_2 (and_2_out, Op[3], Op[2], ~Op[1]);  // AND_Gate
  and and_3 (and_3_out, reversed_1_sign_bit, Op[0]);
  Multiplexer #(.width(32)) multiplexer_1 (
    .in0(B), .in1(reversed_1_b_reversed), .out(multiplexer_1_out), .sel(and_2_out), .en(or_1_out));
  or or_1 (or_1_out, and_1_out, and_2_out);
  and and_4 (and_4_out, and_3_out, and_2_out);
  assign bit_extender_1_out = {{4{or_1_out}}, or_1_out};  // Bit_Extender bit_extender_1
  assign and_5_out = bit_extender_1_out & Sa;  // AND_Gate and_5, 5 bits wide
  LeftShift32 leftshift32_1 (.B(multiplexer_1_out), .Sa(and_5_out), .Cin(and_4_out), .C(leftshift32_1_c));
  Reversed reversed_2 (.B(leftshift32_1_c), .B_reversed(reversed_2_b_reversed));  // open: Sign_bit
  Multiplexer #(.width(32), .enable("false")) multiplexer_2 (
    .in0(leftshift32_1_c), .in1(reversed_2_b_reversed), .out(C), .sel(and_2_out));
endmodule

module Reversed (
  input  [31:0] B,
  output [31:0] B_reversed,
  output Sign_bit
);


  assign B_reversed = {B[0], B[1], B[2], B[3], B[4], B[5], B[6], B[7], B[8], B[9], B[10], B[11], B[12], B[13], B[14], B[15], B[16], B[17], B[18], B[19], B[20], B[21], B[22], B[23], B[24], B[25], B[26], B[27], B[28], B[29], B[30], B[31]};
  assign Sign_bit = B[31];
endmodule
